// Logisim project ALU_Milestone_One.circ as structural Verilog
module ALU_Control (
  input  I30,
  input  I14,
  input  I13,
  input  I12,
  input  I6,
  input  I5,
  input  I4,
  output ALU_Ctrl3,
  output ALU_Ctrl2,
  output ALU_Ctrl1,
  output ALU_Ctrl0,
  output ALU_Src
);

  wire and_2_out, not_1_out, not_2_out, not_3_out, not_4_out, not_5_out;

  not not_1 (not_1_out, I14);
  not not_2 (not_2_out, I13);
  not not_3 (not_3_out, I12);
  not not_4 (not_4_out, I5);
  not not_5 (not_5_out, I4);
  and and_1 (ALU_Ctrl2, I30, not_2_out, I5);
  or or_1 (ALU_Ctrl1, not_2_out, not_5_out);
  and and_2 (and_2_out, I13, not_3_out);
  or or_2 (ALU_Src, not_4_out, not_5_out);
  or or_3 (ALU_Ctrl0, not_1_out, and_2_out);

  assign ALU_Ctrl3 = 1'b0;
endmodule

module one_bit_adder (
  input  A,
  input  B,
  input  C_IN,
  output S,
  output C_OUT
);

  wire and_1_out, and_2_out, xor_1_out;

  xor xor_1 (xor_1_out, A, B);
  xor xor_2 (S, xor_1_out, C_IN);
  and and_1 (and_1_out, xor_1_out, C_IN);
  and and_2 (and_2_out, A, B);
  or or_1 (C_OUT, and_1_out, and_2_out);
endmodule

module one_bit_ALU (
  input  [3:0] ALU_Ctrl,
  input  A,
  input  B,
  input  C_IN,
  output R,
  output C_OUT
);

  wire and_1_out, multiplexer_1_out, not_1_out, one_bit_adder_1_s, or_1_out, xor_1_out;

  not not_1 (not_1_out, B);
  Multiplexer #(.enable("false")) multiplexer_1 (.in0(B), .in1(not_1_out), .out(multiplexer_1_out), .sel(ALU_Ctrl[2]));
  and and_1 (and_1_out, A, multiplexer_1_out);
  or or_1 (or_1_out, A, multiplexer_1_out);
  xor xor_1 (xor_1_out, A, multiplexer_1_out);
  one_bit_adder one_bit_adder_1 (.A(A), .B(multiplexer_1_out), .C_IN(C_IN), .S(one_bit_adder_1_s), .C_OUT(C_OUT));
  Multiplexer #(.enable("false"), .select(2)) multiplexer_2 (
    .in0(and_1_out), .in1(or_1_out), .in2(xor_1_out), .in3(one_bit_adder_1_s), .out(R), .sel(ALU_Ctrl[1:0]));
endmodule

module four_bit_ALU (
  input  [3:0] ALU_Ctrl,
  input  [3:0] A,
  input  [3:0] B,
  input  C_IN,
  output [3:0] R,
  output C_OUT
);

  wire one_bit_alu_1_c_out, one_bit_alu_2_c_out, one_bit_alu_3_c_out;

  one_bit_ALU one_bit_alu_1 (
    .ALU_Ctrl(ALU_Ctrl), .A(A[0]), .B(B[0]), .C_IN(C_IN), .R(R[0]), .C_OUT(one_bit_alu_1_c_out));
  one_bit_ALU one_bit_alu_2 (
    .ALU_Ctrl(ALU_Ctrl), .A(A[1]), .B(B[1]), .C_IN(one_bit_alu_1_c_out), .R(R[1]), .C_OUT(one_bit_alu_2_c_out));
  one_bit_ALU one_bit_alu_3 (
    .ALU_Ctrl(ALU_Ctrl), .A(A[2]), .B(B[2]), .C_IN(one_bit_alu_2_c_out), .R(R[2]), .C_OUT(one_bit_alu_3_c_out));
  one_bit_ALU one_bit_alu_4 (
    .ALU_Ctrl(ALU_Ctrl), .A(A[3]), .B(B[3]), .C_IN(one_bit_alu_3_c_out), .R(R[3]), .C_OUT(C_OUT));
endmodule

module thirty_two_bit_ALU (
  input  [3:0] ALU_Ctrl,
  input  [31:0] A,
  input  [31:0] B,
  output [31:0] R,
  output C_OUT
);

  wire four_bit_alu_1_c_out, four_bit_alu_2_c_out, four_bit_alu_3_c_out, four_bit_alu_4_c_out,
       four_bit_alu_5_c_out, four_bit_alu_6_c_out, four_bit_alu_7_c_out;

  four_bit_ALU four_bit_alu_1 (
    .ALU_Ctrl(ALU_Ctrl), .A(A[3:0]), .B(B[3:0]), .C_IN(ALU_Ctrl[2]), .R(R[3:0]), .C_OUT(four_bit_alu_1_c_out));
  four_bit_ALU four_bit_alu_2 (
    .ALU_Ctrl(ALU_Ctrl), .A(A[7:4]), .B(B[7:4]), .C_IN(four_bit_alu_1_c_out), .R(R[7:4]),
    .C_OUT(four_bit_alu_2_c_out));
  four_bit_ALU four_bit_alu_3 (
    .ALU_Ctrl(ALU_Ctrl), .A(A[11:8]), .B(B[11:8]), .C_IN(four_bit_alu_2_c_out), .R(R[11:8]),
    .C_OUT(four_bit_alu_3_c_out));
  four_bit_ALU four_bit_alu_4 (
    .ALU_Ctrl(ALU_Ctrl), .A(A[15:12]), .B(B[15:12]), .C_IN(four_bit_alu_3_c_out), .R(R[15:12]),
    .C_OUT(four_bit_alu_4_c_out));
  four_bit_ALU four_bit_alu_5 (
    .ALU_Ctrl(ALU_Ctrl), .A(A[19:16]), .B(B[19:16]), .C_IN(four_bit_alu_4_c_out), .R(R[19:16]),
    .C_OUT(four_bit_alu_5_c_out));
  four_bit_ALU four_bit_alu_6 (
    .ALU_Ctrl(ALU_Ctrl), .A(A[23:20]), .B(B[23:20]), .C_IN(four_bit_alu_5_c_out), .R(R[23:20]),
    .C_OUT(four_bit_alu_6_c_out));
  four_bit_ALU four_bit_alu_7 (
    .ALU_Ctrl(ALU_Ctrl), .A(A[27:24]), .B(B[27:24]), .C_IN(four_bit_alu_6_c_out), .R(R[27:24]),
    .C_OUT(four_bit_alu_7_c_out));
  four_bit_ALU four_bit_alu_8 (
    .ALU_Ctrl(ALU_Ctrl), .A(A[31:28]), .B(B[31:28]), .C_IN(four_bit_alu_7_c_out), .R(R[31:28]), .C_OUT(C_OUT));
endmodule

module thirty_two_bit_reg (
  input  [1:0] Read_Register1,
  input  [1:0] Read_Register2,
  input  [31:0] Write_Data,
  input  Clock_In,
  input  Write,
  input  [1:0] Write_Register,
  output [31:0] Read_Data1,
  output [31:0] Read_Data2
);

  wire demultiplexer_1_out0, demultiplexer_1_out1, demultiplexer_1_out2, demultiplexer_1_out3, undriven,
       undriven_2;
  wire [31:0] register_1_q, register_2_q, register_3_q, register_4_q;

  Demultiplexer #(.enable("false"), .select(2)) demultiplexer_1 (
    .out0(demultiplexer_1_out0), .out1(demultiplexer_1_out1), .out2(demultiplexer_1_out2),
    .out3(demultiplexer_1_out3), .in(Write), .sel(Write_Register));
  Register #(.width(32)) register_1 (
    .D(Write_Data), .en(demultiplexer_1_out0), .clk(Clock_In), .Q(register_1_q), .clr(Write));
  Register #(.width(32)) register_2 (
    .D(Write_Data), .en(demultiplexer_1_out1), .clk(Clock_In), .Q(register_2_q), .clr(undriven));
  Register #(.width(32)) register_3 (
    .D(Write_Data), .en(demultiplexer_1_out2), .clk(Clock_In), .Q(register_3_q), .clr(undriven_2));
  Register #(.width(32)) register_4 (
    .D(Write_Data), .en(demultiplexer_1_out3), .clk(Clock_In), .Q(register_4_q));  // open: clr
  Multiplexer #(.enable("false"), .select(2), .width(32)) multiplexer_1 (
    .in0(register_1_q), .in1(register_2_q), .in2(register_3_q), .in3(register_4_q), .out(Read_Data1),
    .sel(Read_Register1));
  Multiplexer #(.enable("false"), .select(2), .width(32)) multiplexer_2 (
    .in0(register_2_q), .in1(register_1_q), .in2(register_3_q), .in3(register_4_q), .out(Read_Data2),
    .sel(Read_Register2));
endmodule

module Register_File (
  input  [4:0] Read_Register1,
  input  [4:0] Read_Register2,
  input  [31:0] Write_Data,
  input  Clock_In,
  input  [4:0] Write_Register,
  input  Write,
  output [31:0] Read_Data1,
  output [31:0] Read_Data2
);

  wire Write3_0, Write7_4, Write11_8, Write15_12, Write19_16, Write23_20, Write27_24, Write31_28;
  wire [31:0] thirty_two_bit_reg2_1_read_data1, thirty_two_bit_reg2_1_read_data2,
       thirty_two_bit_reg2_2_read_data1, thirty_two_bit_reg2_2_read_data2, thirty_two_bit_reg2_3_read_data1,
       thirty_two_bit_reg2_3_read_data2, thirty_two_bit_reg2_4_read_data1, thirty_two_bit_reg2_4_read_data2,
       thirty_two_bit_reg2_5_read_data1, thirty_two_bit_reg2_5_read_data2, thirty_two_bit_reg2_6_read_data1,
       thirty_two_bit_reg2_6_read_data2, thirty_two_bit_reg2_7_read_data1, thirty_two_bit_reg2_7_read_data2,
       thirty_two_bit_reg_1_read_data1, thirty_two_bit_reg_1_read_data2;

  Demultiplexer #(.enable("false"), .select(3)) demultiplexer_1 (
    .out0(Write3_0), .out1(Write7_4), .out2(Write11_8), .out3(Write15_12), .out4(Write19_16),
    .out5(Write23_20), .out6(Write27_24), .out7(Write31_28), .in(Write), .sel(Write_Register[4:2]));
  thirty_two_bit_reg thirty_two_bit_reg_1 (
    .Read_Register1(Read_Register1[1:0]), .Read_Register2(Read_Register2[1:0]), .Write_Data(Write_Data),
    .Clock_In(Clock_In), .Write(Write3_0), .Write_Register(Write_Register[1:0]),
    .Read_Data1(thirty_two_bit_reg_1_read_data1), .Read_Data2(thirty_two_bit_reg_1_read_data2));
  thirty_two_bit_reg2 thirty_two_bit_reg2_1 (
    .Read_Register1(Read_Register1[1:0]), .Read_Register2(Read_Register2[1:0]), .Write_Data(Write_Data),
    .Clock_In(Clock_In), .Write(Write7_4), .Write_Register(Write_Register[1:0]),
    .Read_Data1(thirty_two_bit_reg2_1_read_data1), .Read_Data2(thirty_two_bit_reg2_1_read_data2));
  thirty_two_bit_reg2 thirty_two_bit_reg2_2 (
    .Read_Register1(Read_Register1[1:0]), .Read_Register2(Read_Register2[1:0]), .Write_Data(Write_Data),
    .Clock_In(Clock_In), .Write(Write11_8), .Write_Register(Write_Register[1:0]),
    .Read_Data1(thirty_two_bit_reg2_2_read_data1), .Read_Data2(thirty_two_bit_reg2_2_read_data2));
  thirty_two_bit_reg2 thirty_two_bit_reg2_3 (
    .Read_Register1(Read_Register1[1:0]), .Read_Register2(Read_Register2[1:0]), .Write_Data(Write_Data),
    .Clock_In(Clock_In), .Write(Write15_12), .Write_Register(Write_Register[1:0]),
    .Read_Data1(thirty_two_bit_reg2_3_read_data1), .Read_Data2(thirty_two_bit_reg2_3_read_data2));
  thirty_two_bit_reg2 thirty_two_bit_reg2_4 (
    .Read_Register1(Read_Register1[1:0]), .Read_Register2(Read_Register2[1:0]), .Write_Data(Write_Data),
    .Clock_In(Clock_In), .Write(Write19_16), .Write_Register(Write_Register[1:0]),
    .Read_Data1(thirty_two_bit_reg2_4_read_data1), .Read_Data2(thirty_two_bit_reg2_4_read_data2));
  thirty_two_bit_reg2 thirty_two_bit_reg2_5 (
    .Read_Register1(Read_Register1[1:0]), .Read_Register2(Read_Register2[1:0]), .Write_Data(Write_Data),
    .Clock_In(Clock_In), .Write(Write23_20), .Write_Register(Write_Register[1:0]),
    .Read_Data1(thirty_two_bit_reg2_5_read_data1), .Read_Data2(thirty_two_bit_reg2_5_read_data2));
  thirty_two_bit_reg2 thirty_two_bit_reg2_6 (
    .Read_Register1(Read_Register1[1:0]), .Read_Register2(Read_Register2[1:0]), .Write_Data(Write_Data),
    .Clock_In(Clock_In), .Write(Write27_24), .Write_Register(Write_Register[1:0]),
    .Read_Data1(thirty_two_bit_reg2_6_read_data1), .Read_Data2(thirty_two_bit_reg2_6_read_data2));
  thirty_two_bit_reg2 thirty_two_bit_reg2_7 (
    .Read_Register1(Read_Register1[1:0]), .Read_Register2(Read_Register2[1:0]), .Write_Data(Write_Data),
    .Clock_In(Clock_In), .Write(Write31_28), .Write_Register(Write_Register[1:0]),
    .Read_Data1(thirty_two_bit_reg2_7_read_data1), .Read_Data2(thirty_two_bit_reg2_7_read_data2));
  Multiplexer #(.enable("false"), .select(3), .width(32)) multiplexer_1 (
    .in0(thirty_two_bit_reg_1_read_data1), .in1(thirty_two_bit_reg2_1_read_data1),
    .in2(thirty_two_bit_reg2_2_read_data1), .in3(thirty_two_bit_reg2_3_read_data1),
    .in4(thirty_two_bit_reg2_4_read_data1), .in5(thirty_two_bit_reg2_5_read_data1),
    .in6(thirty_two_bit_reg2_6_read_data1), .in7(thirty_two_bit_reg2_7_read_data1), .out(Read_Data1),
    .sel(Read_Register1[4:2]));
  Multiplexer #(.enable("false"), .select(3), .width(32)) multiplexer_2 (
    .in0(thirty_two_bit_reg_1_read_data2), .in1(thirty_two_bit_reg2_1_read_data2),
    .in2(thirty_two_bit_reg2_2_read_data2), .in3(thirty_two_bit_reg2_3_read_data2),
    .in4(thirty_two_bit_reg2_4_read_data2), .in5(thirty_two_bit_reg2_5_read_data2),
    .in6(thirty_two_bit_reg2_6_read_data2), .in7(thirty_two_bit_reg2_7_read_data2), .out(Read_Data2),
    .sel(Read_Register2[4:2]));
endmodule

module thirty_two_bit_reg2 (
  input  [1:0] Read_Register1,
  input  [1:0] Read_Register2,
  input  [31:0] Write_Data,
  input  Clock_In,
  input  Write,
  input  [1:0] Write_Register,
  output [31:0] Read_Data1,
  output [31:0] Read_Data2
);

  wire demultiplexer_1_out0, demultiplexer_1_out1, demultiplexer_1_out2, demultiplexer_1_out3, undriven,
       undriven_2;
  wire [31:0] register_1_q, register_2_q, register_3_q, register_4_q;

  Demultiplexer #(.enable("false"), .select(2)) demultiplexer_1 (
    .out0(demultiplexer_1_out0), .out1(demultiplexer_1_out1), .out2(demultiplexer_1_out2),
    .out3(demultiplexer_1_out3), .in(Write), .sel(Write_Register));
  Register #(.width(32)) register_1 (
    .D(Write_Data), .en(demultiplexer_1_out0), .clk(Clock_In), .Q(register_1_q));  // open: clr
  Register #(.width(32)) register_2 (
    .D(Write_Data), .en(demultiplexer_1_out1), .clk(Clock_In), .Q(register_2_q), .clr(undriven));
  Register #(.width(32)) register_3 (
    .D(Write_Data), .en(demultiplexer_1_out2), .clk(Clock_In), .Q(register_3_q), .clr(undriven_2));
  Register #(.width(32)) register_4 (
    .D(Write_Data), .en(demultiplexer_1_out3), .clk(Clock_In), .Q(register_4_q));  // open: clr
  Multiplexer #(.enable("false"), .select(2), .width(32)) multiplexer_1 (
    .in0(register_1_q), .in1(register_2_q), .in2(register_3_q), .in3(register_4_q), .out(Read_Data1),
    .sel(Read_Register1));
  Multiplexer #(.enable("false"), .select(2), .width(32)) multiplexer_2 (
    .in0(register_2_q), .in1(register_1_q), .in2(register_3_q), .in3(register_4_q), .out(Read_Data2),
    .sel(Read_Register2));
endmodule

module Milestone2 (
  input  [31:0] Instruction
);

  wire alu_control_1_alu_src, clock_1_out;
  wire [3:0] alu_control_1_alu_ctrl0;
  wire [31:0] bit_extender_1_out, multiplexer_1_out, register_file_1_read_data1, register_file_1_read_data2,
       thirty_two_bit_alu_1_r;

  Clock clock_1 (.out(clock_1_out));
  assign bit_extender_1_out = {{20{Instruction[31]}}, Instruction[31:20]};  // Bit_Extender bit_extender_1
  Register_File register_file_1 (
    .Read_Register1(Instruction[19:15]), .Read_Register2(Instruction[24:20]),
    .Write_Data(thirty_two_bit_alu_1_r), .Clock_In(clock_1_out), .Write_Register(Instruction[11:7]),
    .Write(1'b1), .Read_Data1(register_file_1_read_data1), .Read_Data2(register_file_1_read_data2));
  ALU_Control alu_control_1 (
    .I30(Instruction[30]), .I14(Instruction[14]), .I13(Instruction[13]), .I12(Instruction[12]),
    .I6(Instruction[6]), .I5(Instruction[5]), .I4(Instruction[4]), .ALU_Ctrl3(alu_control_1_alu_ctrl0[3]),
    .ALU_Ctrl2(alu_control_1_alu_ctrl0[2]), .ALU_Ctrl1(alu_control_1_alu_ctrl0[1]),
    .ALU_Ctrl0(alu_control_1_alu_ctrl0[0]), .ALU_Src(alu_control_1_alu_src));
  Multiplexer #(.enable("false"), .width(32)) multiplexer_1 (
    .in0(register_file_1_read_data2), .in1(bit_extender_1_out), .out(multiplexer_1_out),
    .sel(alu_control_1_alu_src));
  thirty_two_bit_ALU thirty_two_bit_alu_1 (
    .ALU_Ctrl(alu_control_1_alu_ctrl0), .A(register_file_1_read_data1), .B(multiplexer_1_out),
    .R(thirty_two_bit_alu_1_r));  // open: C_OUT
endmodule
